# Fritzing sketch main (saved by Fritzing 0.9.2b)
breadboards: 1

parts:
  Raspberry_Pi_2 = Raspberry Pi 2
  Port3 = shrouded pin header, 6 pins [form="♂ (shrouded male)"]
  Port2 = shrouded pin header, 6 pins [form="♂ (shrouded male)"]
  Port1 = shrouded pin header, 6 pins [form="♂ (shrouded male)"]
  GPS = female pin header, 9 pins [form="♀ (female)"]
  M2 = male pin header, 2 pins [form="♂ (male)"]
  M3 = male pin header, 2 pins [form="♂ (male)"]
  M4 = male pin header, 2 pins [form="♂ (male)"]
  M1 = male pin header, 2 pins [form="♂ (male)"]
  A3 = male pin header, 3 pins [form="♂ (male)"]
  A2 = male pin header, 3 pins [form="♂ (male)"]
  A1 = male pin header, 3 pins [form="♂ (male)"]
  A0 = male pin header, 3 pins [form="♂ (male)"]
  J1 = female pin header, 2 pins [form="♀ (female)"]
  J2 = female pin header, 2 pins [form="♀ (female)"]
  Disp = male pin header, 3 pins [form="♂ (male)"]
  Port4 = shrouded pin header, 6 pins [form="♂ (shrouded male)"]
  U4 = SSOP20 [chip_label=74LVC244 package=SSOP]
  R1 = Resistor [tolerance=±1% resistance=10k package="0805 [SMD]"]
  R2 = Resistor [tolerance=±1% resistance=100k package="0805 [SMD]"]
  R3 = Resistor [tolerance=±1% resistance=10k package="0805 [SMD]"]
  R4 = Resistor [tolerance=±1% resistance=10k package="0805 [SMD]"]
  R7 = Resistor [tolerance=±1% resistance=10k package="0805 [SMD]"]
  R6 = Resistor [tolerance=±1% resistance=10k package="0805 [SMD]"]
  R5 = Resistor [tolerance=±1% resistance=10k package="0805 [SMD]"]
  C4 = Ceramic Capacitor [capacitance=100nF package="0805 [SMD, multilayer]"]
  C3 = Ceramic Capacitor [capacitance=100nF package="0805 [SMD, multilayer]"]
  C2 = Ceramic Capacitor [capacitance=22pF package="0805 [SMD, multilayer]"]
  C1 = Ceramic Capacitor [capacitance=22pF package="0805 [SMD, multilayer]"]
  Q3 = MOSFET-NCHANNEL [package=sot23-3]
  Q2 = MOSFET-NCHANNEL [package=sot23-3]
  Q1 = MOSFET-NCHANNEL [package=sot23-3]
  XTAL1 = Crystal [frequency="16 Mhz" package=THT]
  U3 = LT3514 [package=tssop-24]
  C5 = Ceramic Capacitor [capacitance=1µF package="0805 [SMD, multilayer]"]
  L1 = Inductor [inductance=10µH package="0805 [SMD]"]
  L2 = Inductor [inductance=4.7µH package="400 mil [THT]"]
  D1 = DIODE-SCHOTTKY [package=sma-diode]
  LED1 = Tri-Color LED SMD [package=led-tricolor-smd]  # not connected
  C9 = Ceramic Capacitor [capacitance=47pF package="0805 [SMD, multilayer]"]
  C6 = Ceramic Capacitor [capacitance=1µF package="0805 [SMD, multilayer]"]
  C7 = Ceramic Capacitor [capacitance=1µF package="0805 [SMD, multilayer]"]
  C8 = Ceramic Capacitor [capacitance=47nF package="0805 [SMD, multilayer]"]
  R8 = Resistor [tolerance=±1% resistance=18.2k package="1206 [SMD]"]
  R9 = Resistor [tolerance=±1% resistance=31.6k package="0805 [SMD]"]
  C10 = Ceramic Capacitor [capacitance=47µF package="0805 [SMD, multilayer]"]
  R10 = Resistor [tolerance=±1% resistance=10.2k package="0805 [SMD]"]
  D2 = DIODE-SCHOTTKY [package=sma-diode]
  L3 = Inductor [inductance=8.2µH package="400 mil [THT]"]
  C11 = Ceramic Capacitor [capacitance=22pF package="0805 [SMD, multilayer]"]
  R11 = Resistor [tolerance=±1% resistance=53.6k package="0805 [SMD]"]
  C12 = Ceramic Capacitor [capacitance=22µF package="0805 [SMD, multilayer]"]
  R12 = Resistor [tolerance=±1% resistance=10.2k package="0805 [SMD]"]
  D3 = DIODE-SCHOTTKY [package=sma-diode]
  L4 = Inductor [inductance=8.2µH package="400 mil [THT]"]
  C13 = Ceramic Capacitor [capacitance=22pF package="0805 [SMD, multilayer]"]
  R13 = Resistor [tolerance=±1% resistance=53.6k package="0805 [SMD]"]
  C14 = Ceramic Capacitor [capacitance=22µF package="0805 [SMD, multilayer]"]
  R14 = Resistor [tolerance=±1% resistance=10.2k package="0805 [SMD]"]
  PWR = male pin header, 4 pins [form="♂ (male)"]
  Q4 = MOSFET-NCHANNEL [package=sot23-3]
  Q5 = MOSFET-NCHANNEL [package=sot23-3]
  R15 = Resistor [tolerance=±1% resistance=100k package="0805 [SMD]"]
  R16 = Resistor [tolerance=±1% resistance=100k package="0805 [SMD]"]
  U2 = SOIC-14 [chip_label=ATTINY24 package=SO]
  C15 = Ceramic Capacitor [capacitance=47nF package="0805 [SMD, multilayer]"]
  C16 = Ceramic Capacitor [capacitance=47nF package="0805 [SMD, multilayer]"]
  C17 = Ceramic Capacitor [capacitance=100nF package="0805 [SMD, multilayer]"]
  R17 = Resistor [tolerance=±1% resistance=220 package="0805 [SMD]"]
  R18 = Resistor [tolerance=±1% resistance=220 package="0805 [SMD]"]
  R19 = Resistor [tolerance=±1% resistance=10k package="0805 [SMD]"]
  Q6 = MOSFET-NCHANNEL [package=sot23-3]
  R20 = Resistor [tolerance=±1% resistance=100k package="0805 [SMD]"]
  ISP2 = double row male pin header, 6 pins [form="♂ (male)"]
  ISP1 = double row male pin header, 6 pins [form="♂ (male)"]
  NEOPIXEL1 = Neopixel Strip -- Black (30/m)  # not connected
  U1 = atmega168 smd [package=tqfp]

nets:
  3.3V_SDA: Raspberry_Pi_2.GPIO2, R4.Pin_0, Q2.S
  3.3V_SCL: Raspberry_Pi_2.GPIO3, R5.Pin_0, Q3.S
  PI_MOSI: Raspberry_Pi_2.GPIO10, U4.6, U4.15
  PI_MISO: Raspberry_Pi_2.GPIO9, U4.3, U4.12
  PI_SCK: Raspberry_Pi_2.GPIO11, U4.4, U4.13
  GND: Raspberry_Pi_2.GND, Port3.pin3, Port3.pin6, Port2.pin3, Port2.pin6, Port1.pin3, Port1.pin6, GPS.pin7, A3.pin3, A2.pin3, A1.pin3, A0.pin3, Disp.pin3, Port4.pin3, Port4.pin6, U4.10, R2.Pin_0, C4.1, C2.0, C1.0, Q1.S, U3.GND, C6.0, C7.0, C8.0, R8.Pin_0, C10.0, R10.Pin_1, C12.0, R12.Pin_1, C14.0, R14.Pin_1, PWR.pin4, Q4.S, Q5.S, R15.Pin_0, R16.Pin_0, U2.14, C15.0, C16.0, C17.1, R18.Pin_0, Q6.S, R20.Pin_0, ISP2.pin4, ISP1.pin4, U1.Pin_22
  N1: Raspberry_Pi_2.GPIO26, GPS.pin2
  PI_CE1: Raspberry_Pi_2.GPIO7, U4.19, R19.Pin_1
  PI_CE0: Raspberry_Pi_2.GPIO8, U4.1, R1.Pin_0
  N2: Raspberry_Pi_2.GPIO15, GPS.pin5, J2.pin1
  N3: Raspberry_Pi_2.GPIO14, GPS.pin6, J1.pin1
  5V: Port3.pin1, Port2.pin1, Port1.pin1, A3.pin2, A2.pin2, A1.pin2, A0.pin2, Disp.pin2, Port4.pin1, R3.Pin_0, R7.Pin_1, R6.Pin_1, C4.0, C3.1, L3.pin_1, C11.1, R11.Pin_1, C12.1, ISP1.pin6, U1.Pin_7, U1.Pin_20
  3.3V: Port3.pin2, Port2.pin2, Port1.pin2, GPS.pin1, Port4.pin2, U4.20, R1.Pin_1, R4.Pin_1, R5.Pin_1, Q3.G, Q2.G, L2.pin_1, C9.1, R9.Pin_1, C10.1, R19.Pin_0
  5V_SDA: Port3.pin4, Port2.pin4, Port1.pin4, Port4.pin4, R7.Pin_0, Q2.D, PWR.pin1, U1.Pin_27
  5V_SCL: Port3.pin5, Port2.pin5, Port1.pin5, Port4.pin5, R6.Pin_0, Q3.D, PWR.pin2, U1.Pin_28
  AVR_D4: M2.pin1, U1.Pin_6
  PWM1: M2.pin2, U1.Pin_11
  AVR_D7: M3.pin1, U1.Pin_13
  PWM2: M3.pin2, U1.Pin_12
  AVR_D8: M4.pin1, U1.Pin_14
  PWM3: M4.pin2, U1.Pin_15
  AVR_D2: M1.pin1, U1.Pin_4
  PWM0: M1.pin2, U1.Pin_5
  ADC3: A3.pin1, U1.Pin_26
  ADC2: A2.pin1, U1.Pin_25
  ADC1: A1.pin1, U1.Pin_24
  ADC0: A0.pin1, U1.Pin_23
  AVR_TX: J1.pin2, U1.Pin_3
  AVR_RX: J2.pin2, U1.Pin_2
  N4: Disp.pin1, U1.Pin_16
  U2_MOSI: U4.5, U2.7, ISP2.pin5
  U2_SCK: U4.7, U2.9, ISP2.pin2
  U1_MISO: U4.8, ISP1.pin1, U1.Pin_18
  N5: U4.9, Q6.G, R20.Pin_1
  U1_MOSI: U4.14, ISP1.pin5, U1.Pin_17
  U1_SCK: U4.16, ISP1.pin2, U1.Pin_19
  U2_MISO: U4.17, U2.8, ISP2.pin1
  N6: U4.18, R2.Pin_1, Q1.G
  U1_RST: R3.Pin_1, Q1.D, ISP1.pin3, U1.Pin_1
  N7: C3.0, U1.Pin_8
  N8: C2.1, XTAL1.pin_0, U1.Pin_10
  N9: C1.1, XTAL1.pin_1, U1.Pin_9
  VIN: U3.VIN, U3.EN/UVLO, C5.0, L1.pin_1, C6.1, C7.1, PWR.pin3, R17.Pin_1
  N10: U3.DA3, D2.A
  N11: U3.SW3, D2.C, L3.pin_0
  N12: U3.SW1, L2.pin_0, D1.C
  N13: U3.DA1, D1.A
  N14: U3.SW4, D3.C, L4.pin_0
  N15: U3.DA4, D3.A
  N16: U3.RUN/SS4, C8.1
  3.3V_SHTDWN: U3.RUN/SS1, Q4.D, C16.1
  5V_SHTDWN: U3.RUN/SS3, Q5.D, C15.1
  N17: U3.RT/SNYNC, R8.Pin_1
  N18: U3.FB4, C13.0, R13.Pin_0, R14.Pin_0
  N19: U3.FB1, C9.0, R9.Pin_0, R10.Pin_0
  N20: U3.FB3, C11.0, R11.Pin_0, R12.Pin_0
  PG: U3.PG, U2.13
  N21: U3.SW5, L1.pin_0
  N22: U3.SKY, C5.1
  5V_CRITICAL: L4.pin_1, C13.1, R13.Pin_1, C14.1, U2.1, C17.0, ISP2.pin6
  N23: Q4.G, R16.Pin_1, U2.2
  N24: Q5.G, R15.Pin_1, U2.3
  U2_RST: U2.4, Q6.D, ISP2.pin3
  N25: U2.12, R17.Pin_0, R18.Pin_1

notes:
  3.3V
  VBAT
  FIX
  TX
  RX
  GND
  VIN
  PPS
  EN
  I2C Level Shifter
  Raspberry Pi Header
  Analog Sensor & Motion Interface
  AVR Programmer
  ADC Header
  Expansion Ports
  Motors
  5V
  G
  A
  Rx
  E
  Pathfinder v2
  Andy Condon ©2016
  M
  Power Supply
  Power Monitor & Control

custom parts:
  LT3514: Linear Technology LT3514 Triple Step-Down Switching Regulator Three Outputs: 2A, 1A, 1A
  Neopixel Strip -- Black (30/m): These NeoPixel strips have 30 digitally-addressable pixel LEDs per meter and are very affordable and are only 12.5 mm wide, 10 mm if you remove the strip from the casing.
