# Fritzing sketch navigation (saved by Fritzing 0.9.2b)
breadboards: 1

parts:
  U1 = atmega328 [package=dip]
  XTAL1 = Crystal [frequency="16 Mhz" package=THT]
  IC1 = IC, DIP package, 20 pins [chip_label=74LVC244]
  GPS1 = female pin header, 9 pins [form="♀ (female)"]
  Raspberry_Pi_2 = Raspberry Pi 2
  Power = shrouded pin header, 6 pins [form="♂ (shrouded male)"]
  C3 = Ceramic Capacitor [capacitance=100nF package="100 mil [THT, multilayer]"]
  C4 = Ceramic Capacitor [capacitance=100nF package="100 mil [THT, multilayer]"]
  R1 = Resistor [tolerance=±5% resistance=10k package=THT]
  Q1 = MOSFET-NCHANNEL [package=to-92]
  R2 = Resistor [tolerance=±5% resistance=10k package=THT]
  R3 = Resistor [tolerance=±5% resistance=100k package=THT]
  C5 = Ceramic Capacitor [capacitance=22pF package="100 mil [THT, multilayer]"]
  C1 = Ceramic Capacitor [capacitance=22pF package="100 mil [THT, multilayer]"]
  Q4 = MOSFET-NCHANNEL [package=to-92]
  Q5 = MOSFET-NCHANNEL [package=to-92]
  R6 = Resistor [tolerance=±5% resistance=10k package=THT]
  R7 = Resistor [tolerance=±5% resistance=10k package=THT]
  R8 = Resistor [tolerance=±5% resistance=10k package=THT]
  R9 = Resistor [tolerance=±5% resistance=10k package=THT]

nets:
  AVR_RST: U1.RESET, Q1.D, R2.Pin_1
  5V: U1.D4, U1.AVCC, Power.pin1, C3.0, C4.1, R2.Pin_0, R8.Pin_1, R9.Pin_1
  GND: U1.GND, IC1.pin10, IC1.pin11, IC1.pin13, IC1.pin15, IC1.pin17, GPS1.pin7, Raspberry_Pi_2.GND, Power.pin3, Power.pin6, C3.1, C4.0, Q1.S, R3.Pin_0, C5.1, C1.1
  N1: U1.XLAT1, XTAL1.pin_1, C1.0
  N2: U1.XLAT2, XTAL1.pin_0, C5.0
  AVR_MOSI: U1.D11_(PWM), IC1.pin14
  AVR_MISO: U1.D12, IC1.pin8
  AVR_SCK: U1.D13, IC1.pin16
  5V_SDA: U1.A4, Power.pin4, Q5.D, R9.Pin_0
  5V_SCL: U1.A5, Power.pin5, Q4.D, R8.Pin_0
  PI_CE0: IC1.pin1, Raspberry_Pi_2.GPIO8, R1.Pin_0
  PI_SCK: IC1.pin4, Raspberry_Pi_2.GPIO11
  PI_MOSI: IC1.pin6, Raspberry_Pi_2.GPIO10
  PI_MISO: IC1.pin12, Raspberry_Pi_2.GPIO9
  N3: IC1.pin18, Q1.G, R3.Pin_1
  3.3V: IC1.pin19, IC1.pin20, GPS1.pin1, Power.pin2, R1.Pin_1, Q4.G, Q5.G, R6.Pin_1, R7.Pin_1
  N4: GPS1.pin5, Raspberry_Pi_2.GPIO15
  N5: GPS1.pin6, Raspberry_Pi_2.GPIO14
  3.3V_SDA: Raspberry_Pi_2.GPIO2, Q5.S, R6.Pin_0
  3.3V_SCL: Raspberry_Pi_2.GPIO3, Q4.S, R7.Pin_0

notes:
  3.3V
  VBAT
  FIX
  TX
  RX
  GND
  VIN
  PPS
  EN
  I2C SCL
  I2C SDA
  5V
  I2C Level Shifter
  Raspberry Pi Header
  Atmel ATMEGA 328p
  ATMEGA Programmer
