# Fritzing sketch navigator (saved by Fritzing 0.9.2b)
breadboards: 1

parts:
  U1 = atmega328 [package=dip]
  XTAL1 = Crystal [frequency="16 Mhz" package=THT]
  IC1 = IC, DIP package, 20 pins [chip_label=74LVC244]
  GPS1 = female pin header, 9 pins [form="♀ (female)"]
  Raspberry_Pi_2 = Raspberry Pi 2
  Power = shrouded pin header, 6 pins [form="♂ (shrouded male)"]
  C1 = Ceramic Capacitor [capacitance=22pF package="100 mil [THT, multilayer]"]
  C2 = Ceramic Capacitor [capacitance=22pF package="100 mil [THT, multilayer]"]
  C3 = Ceramic Capacitor [capacitance=100nF package="100 mil [THT, multilayer]"]
  C4 = Ceramic Capacitor [capacitance=100nF package="100 mil [THT, multilayer]"]

nets:
  N1: U1.VCC, U1.AVCC, Power.pin1, C3.0, C4.1
  N2: U1.GND, IC1.pin10, IC1.pin11, IC1.pin13, IC1.pin15, IC1.pin17, GPS1.pin7, Power.pin3, Power.pin6, C1.1, C2.0, C3.1, C4.0
  N3: U1.XLAT1, XTAL1.pin_1, C1.0
  N4: U1.XLAT2, XTAL1.pin_0, C2.1
  N5: GPS1.pin5, Raspberry_Pi_2.GPIO15
  N6: GPS1.pin6, Raspberry_Pi_2.GPIO14
  GND: Raspberry_Pi_2.GND

notes:
  3.3V
  VBAT
  FIX
  TX
  RX
  GND
  VIN
  PPS
  EN
  BAT2 LVL
  BAT1 LVL
  5V
